// Logisim project s-mips.circ as structural Verilog: 19 circuits, main circuit S-MIPS Board
module S_MIPS_Board (
  input  DESHABILITAR_DISPATCHER,
  output halt
);

  wire button_1_out, CLK, CS, d_ff_1_q, LCLR, LoadRAM, LoadRAMOn, LW, R_R_W, R_W, ram_dispatcher_1_finished,
       RCS, Reset_out, RST, TTY_EN;
  wire [2:0] KDB;
  wire [3:0] LMask, Mask, ram_1_read_time, ram_1_write_time, RMask;
  wire [6:0] KDB_DATA, TTY_DATA;
  wire [15:0] Addr, LAddr, RAddr;
  wire [31:0] I0, I1, I2, I3, LData, ram_1_data_out_0, ram_1_data_out_1, ram_1_data_out_2, ram_1_data_out_3,
       RI0, RI1, RI2, RI3;

  TTY #(.rows(25), .cols(80)) tty_1 (.data(TTY_DATA), .clk(CLK), .we(TTY_EN), .clr(RST));
  not not_1 (LoadRAMOn, ram_dispatcher_1_finished);
  RAM_Dispatcher ram_dispatcher_1 (
    .WriteTime(ram_1_write_time), .Clock(CLK), .Data(LData), .Address(LAddr), .Mask(LMask),
    .Finished(ram_dispatcher_1_finished), .Write(LW), .CLR(LCLR));
  Keyboard #(.buflen(64)) keyboard_1 (.clk(CLK), .re(KDB[0]), .avail(KDB[2]), .data(KDB_DATA));  // open: clr
  RAM ram_1 (
    .Address(RAddr), .Data_Out_0(ram_1_data_out_0), .Data_Out_1(ram_1_data_out_1),
    .Data_Out_2(ram_1_data_out_2), .Data_Out_3(ram_1_data_out_3), .Data_In_0(RI0), .Data_In_1(RI1),
    .Data_In_2(RI2), .Data_In_3(RI3), .Mask(RMask), .nRead_Write(R_R_W), .Chip_Select(RCS),
    .Read_Time(ram_1_read_time), .Reset(button_1_out), .Write_Time(ram_1_write_time));
  Button button_1 (.out(button_1_out));
  D_Flip_Flop d_ff_1 (.clk(CLK), .D(1'b1), .Q(d_ff_1_q), .reset(Reset_out));  // open: Qn, preset, en
  Button Reset (.out(Reset_out));
  S_MIPS s_mips_1 (
    .Kbd_Enable(KDB[0]), .Address(Addr), .Kbd_Clear(KDB[1]), .Kbd_Available(KDB[2]), .RAM_In_0(I0),
    .Kbd_ASCII_Data(KDB_DATA), .RAM_In_1(I1), .TTY_Enable(TTY_EN), .RAM_In_2(I2), .RAM_In_3(I3),
    .TTY_ASCII_Data(TTY_DATA), .Reset(RST), .RAM_Out_0(ram_1_data_out_0), .Clock(CLK),
    .RAM_Out_1(ram_1_data_out_1), .Stop(halt), .RAM_Out_2(ram_1_data_out_2), .RAM_Out_3(ram_1_data_out_3),
    .Mask(Mask), .Read_Time(ram_1_read_time), .Write_Time(ram_1_write_time), .nRead_Write(R_W),
    .Chip_Select(CS));
  D_Flip_Flop d_ff_2 (.clk(CLK), .D(d_ff_1_q), .Qn(LCLR), .reset(Reset_out));  // open: Q, preset, en
  or or_1 (RST, LCLR, LoadRAM);
  Clock clock_1 (.out(CLK));
  Multiplexer #(.width(32), .enable("false")) multiplexer_1 (.in0(I0), .in1(LData), .out(RI0), .sel(LoadRAM));
  Multiplexer #(.width(32), .enable("false")) multiplexer_2 (.in0(I1), .in1(LData), .out(RI1), .sel(LoadRAM));
  Multiplexer #(.width(32), .enable("false")) multiplexer_3 (.in0(I2), .in1(LData), .out(RI2), .sel(LoadRAM));
  Multiplexer #(.width(32), .enable("false")) multiplexer_4 (.in0(I3), .in1(LData), .out(RI3), .sel(LoadRAM));
  and and_1 (LoadRAM, ~DESHABILITAR_DISPATCHER, LoadRAMOn);  // AND_Gate
  Multiplexer #(.width(16), .enable("false")) multiplexer_5 (.in0(Addr), .in1(LAddr), .out(RAddr), .sel(LoadRAM));
  Multiplexer #(.width(4), .enable("false")) multiplexer_6 (.in0(Mask), .in1(LMask), .out(RMask), .sel(LoadRAM));
  Multiplexer #(.enable("false")) multiplexer_7 (.in0(CS), .in1(LW), .out(RCS), .sel(LoadRAM));
  Multiplexer #(.enable("false")) multiplexer_8 (.in0(R_W), .in1(LW), .out(R_R_W), .sel(LoadRAM));

  // Notes on the sheet:
  //   NO MODIFICAR
  //   Keyboard
endmodule

module RAM (
  input  [15:0] Address,
  input  [31:0] Data_In_0,
  input  [31:0] Data_In_1,
  input  [31:0] Data_In_2,
  input  [31:0] Data_In_3,
  input  [3:0] Mask,
  input  nRead_Write,
  input  Chip_Select,
  input  Reset,
  output [31:0] Data_Out_0,
  output [31:0] Data_Out_1,
  output [31:0] Data_Out_2,
  output [31:0] Data_Out_3,
  output [3:0] Read_Time,
  output [3:0] Write_Time
);

  wire and_2_out, and_3_out, and_4_out, and_5_out, and_6_out, and_7_out, and_8_out, and_9_out, Changed, CLK,
       comparator_2_eq, comparator_3_eq, comparator_4_eq, comparator_5_eq, comparator_6_eq, Count,
       demultiplexer_3_out0, Idle, Idle_q, Load, Load0, Load1, nand_1_out, or_1_out, or_2_out, or_3_out,
       or_4_out, or_5_out, or_6_out, or_7_out, or_8_out, or_9_out, or_10_out, Proc_q, Update_Mem, Zero_Time;
  wire [3:0] counter_1_q, multiplexer_1_out, subtractor_1_out;
  wire [31:0] register_1_q, register_2_q, register_3_q, register_4_q, register_5_q;

  // Probe on 4'b0011
  // Probe on 4'b0010
  Multiplexer #(.width(4), .enable("false")) multiplexer_1 (
    .in0(4'b0011), .in1(4'b0010), .out(multiplexer_1_out), .sel(nRead_Write));
  or or_1 (or_1_out, Idle, Update_Mem);
  or or_2 (or_2_out, ~Chip_Select, Reset);  // OR_Gate
  Subtractor #(.width(4)) subtractor_1 (.a(multiplexer_1_out), .b(4'b0010), .out(subtractor_1_out));  // open: bin, bout
  Demultiplexer #(.enable("false")) demultiplexer_1 (.out0(Idle), .out1(Load0), .in(Idle_q), .sel(Changed));
  D_Flip_Flop u_Idle (.clk(CLK), .D(or_1_out), .Q(Idle_q), .preset(or_2_out));  // open: Qn, en, reset
  // Probe on counter_1_q
  Counter #(.width(4), .max('hf)) counter_1 (
    .load(Load), .D(subtractor_1_out), .count(Count), .Q(counter_1_q), .clk(CLK), .clr(or_3_out));  // open: carry
  or or_3 (or_3_out, ~Chip_Select, Reset);  // OR_Gate
  Comparator #(.width(4), .mode("unsigned")) comparator_1 (
    .a(4'b0000), .b(counter_1_q), .eq(Zero_Time));  // open: gt, lt
  or or_4 (or_4_out, Count, Load0, Load1);
  Register #(.width(32)) register_1 (.D(Data_In_0), .en(Chip_Select), .Q(register_1_q), .clk(CLK), .clr(or_5_out));
  or or_5 (or_5_out, ~Chip_Select, Reset);  // OR_Gate
  Register #(.width(32)) register_2 (.D(Data_In_1), .en(Chip_Select), .Q(register_2_q), .clk(CLK), .clr(or_6_out));
  or or_6 (or_6_out, ~Chip_Select, Reset);  // OR_Gate
  Register #(.width(32)) register_3 (.D(Data_In_2), .en(Chip_Select), .Q(register_3_q), .clk(CLK), .clr(or_7_out));
  or or_7 (or_7_out, ~Chip_Select, Reset);  // OR_Gate
  Register #(.width(32)) register_4 (.D(Data_In_3), .en(Chip_Select), .Q(register_4_q), .clk(CLK), .clr(or_8_out));
  or or_8 (or_8_out, ~Chip_Select, Reset);  // OR_Gate
  Register #(.width(32)) register_5 (
    .D({{11{1'b1}}, nRead_Write, Mask, Address}), .en(Chip_Select), .Q(register_5_q), .clk(CLK),
    .clr(or_9_out));
  or or_9 (or_9_out, ~Chip_Select, Reset);  // OR_Gate
  D_Flip_Flop Proc (.clk(CLK), .D(or_4_out), .Q(Proc_q), .reset(or_10_out));  // open: Qn, preset, en
  or or_10 (or_10_out, ~Chip_Select, Reset);  // OR_Gate
  Demultiplexer #(.enable("false")) demultiplexer_2 (
    .out0(Count), .out1(Update_Mem), .in(demultiplexer_3_out0), .sel(Zero_Time));
  Demultiplexer #(.enable("false")) demultiplexer_3 (
    .out0(demultiplexer_3_out0), .out1(Load1), .in(Proc_q), .sel(Changed));
  Clock clock_1 (.out(CLK));
  Comparator #(.width(32)) comparator_2 (.a(register_1_q), .b(Data_In_0), .eq(comparator_2_eq));  // open: gt, lt
  Comparator #(.width(32)) comparator_3 (.a(register_2_q), .b(Data_In_1), .eq(comparator_3_eq));  // open: gt, lt
  Comparator #(.width(32)) comparator_4 (.a(register_3_q), .b(Data_In_2), .eq(comparator_4_eq));  // open: gt, lt
  Comparator #(.width(32)) comparator_5 (.a(register_4_q), .b(Data_In_3), .eq(comparator_5_eq));  // open: gt, lt
  Comparator #(.width(32)) comparator_6 (
    .a(register_5_q), .b({{11{1'b1}}, nRead_Write, Mask, Address}), .eq(comparator_6_eq));  // open: gt, lt
  nand nand_1 (nand_1_out, comparator_6_eq, comparator_2_eq, comparator_3_eq, comparator_4_eq, comparator_5_eq);
  and and_1 (Changed, nand_1_out, Chip_Select);
  or or_11 (Load, Count, Load1, Load0);
  and and_2 (and_2_out, Mask[0], Update_Mem, nRead_Write);
  and and_3 (and_3_out, Mask[1], Update_Mem, nRead_Write);
  and and_4 (and_4_out, Mask[2], Update_Mem, nRead_Write);
  and and_5 (and_5_out, Mask[3], Update_Mem, nRead_Write);
  RAM_part #(.addrWidth(16), .dataWidth(32), .bus("separate")) ram_1 (
    .addr(Address), .din(Data_In_0), .data(Data_Out_0), .str(and_2_out), .sel(Chip_Select), .clk(CLK),
    .ld(and_6_out), .clr(Reset));
  and and_6 (and_6_out, ~nRead_Write, Idle);  // AND_Gate
  RAM_part #(.addrWidth(16), .dataWidth(32), .bus("separate")) ram_2 (
    .addr(Address), .din(Data_In_1), .data(Data_Out_1), .str(and_3_out), .sel(Chip_Select), .clk(CLK),
    .ld(and_7_out), .clr(Reset));
  and and_7 (and_7_out, ~nRead_Write, Idle);  // AND_Gate
  RAM_part #(.addrWidth(16), .dataWidth(32), .bus("separate")) ram_3 (
    .addr(Address), .din(Data_In_2), .data(Data_Out_2), .str(and_4_out), .sel(Chip_Select), .clk(CLK),
    .ld(and_8_out), .clr(Reset));
  and and_8 (and_8_out, ~nRead_Write, Idle);  // AND_Gate
  RAM_part #(.addrWidth(16), .dataWidth(32), .bus("separate")) ram_4 (
    .addr(Address), .din(Data_In_3), .data(Data_Out_3), .str(and_5_out), .sel(Chip_Select), .clk(CLK),
    .ld(and_9_out), .clr(Reset));
  and and_9 (and_9_out, ~nRead_Write, Idle);  // AND_Gate

  assign Read_Time = 4'b0011;
  assign Write_Time = 4'b0010;

  // Other names for the same wires on the sheet: M0 = Mask[0]; M1 = Mask[1]; M2 = Mask[2]; M3 = Mask[3];
  //   RW = nRead_Write; CLR = Reset; CS = Chip_Select; Load2 = Count

  // Notes on the sheet:
  //   NO MODIFICAR
  //   excepto quizás los valores RT y WT
  //   BANK0
  //   BANK1
  //   BANK2
  //   BANK3
endmodule

module S_MIPS (
  input  Kbd_Available,
  input  [6:0] Kbd_ASCII_Data,
  input  [31:0] RAM_Out_0,
  input  [31:0] RAM_Out_1,
  input  Reset,
  input  [31:0] RAM_Out_2,
  input  Clock,
  input  [31:0] RAM_Out_3,
  input  [3:0] Read_Time,
  input  [3:0] Write_Time,
  output Kbd_Enable,
  output [15:0] Address,
  output Kbd_Clear,
  output TTY_Enable,
  output [6:0] TTY_ASCII_Data,
  output Stop,
  output [31:0] RAM_In_0,
  output [31:0] RAM_In_1,
  output [31:0] RAM_In_2,
  output [31:0] RAM_In_3,
  output [3:0] Mask,
  output nRead_Write,
  output Chip_Select
);

  wire ALUSrcA, EQF, ExtndSrc, INstr_en, NF, PC_En, result_Load, ValueSrc, WE3, ZF;
  wire [1:0] A3Src, Address_Src, ALUSrcB, Branch_Src;
  wire [2:0] WD3_Src;
  wire [3:0] ALU_Control;
  wire [5:0] Func_Code, Op_Code;
  wire [31:0] Data, Memory_Addresss, Value;

  Read_from_Ram read_from_ram_1 (
    .RAM_DATA(Data), .BANK0(RAM_Out_0), .BANK1(RAM_Out_1), .BANK2(RAM_Out_2), .BANK3(RAM_Out_3),
    .MEMORY(Memory_Addresss));
  Control_Unit control_unit_1 (
    .in_1(Clock), .R_Time(Read_Time), .in_3(Reset), .W_time(Write_Time), .in_5(Op_Code), .in_6(Func_Code),
    .in_7(ZF), .in_8(NF), .in_9(EQF), .Write(nRead_Write), .ALUSrc_A(ALUSrcA), .ALUSrc_B(ALUSrcB),
    .CS(Chip_Select), .Address_Src(Address_Src), .Branch_Src(Branch_Src), .A3Src(A3Src), .WD3Src(WD3_Src),
    .ALU_Control(ALU_Control), .WE3(WE3), .PCEn(PC_En), .TTY_Enable(TTY_Enable), .Stop(Stop),
    .Value_Src(ValueSrc), .Kbd_En(Kbd_Enable), .Instr_En(INstr_en), .ExtendSrc(ExtndSrc),
    .Result_Load(result_Load));
  Data_Path data_path_1 (
    .Clock(Clock), .A3Src(A3Src), .WD3Src(WD3_Src), .Reset(Reset), .ALUControl(ALU_Control),
    .ALUSrcA(ALUSrcA), .ALUSrcB(ALUSrcB), .WriteReg(WE3), .AddressSrc(Address_Src), .PCEnable(PC_En),
    .BranchSrc(Branch_Src), .RamData(Data), .Op_Code(Op_Code), .Func_code(Func_Code),
    .Address(Memory_Addresss), .ZF(ZF), .NF(NF), .EQF(EQF), .Kbd_ASCII_Data(Kbd_ASCII_Data),
    .TTY_DAta(TTY_ASCII_Data), .Value(Value), .Value_Src(ValueSrc), .Kbd_available(Kbd_Available),
    .Instru_En(INstr_en), .ExtendSrc(ExtndSrc), .Result_Load(result_Load));
  Write_to_Ram write_to_ram_1 (
    .ADDRESS(Address), .VALUE(Value), .MASK(Mask), .INPUT0(RAM_In_0), .INPUT1(RAM_In_1), .INPUT2(RAM_In_2),
    .INPUT3(RAM_In_3), .MEMORY(Memory_Addresss));

  assign Kbd_Clear = Reset;

  // Other names for the same wires on the sheet: CLK = Clock; CS = Chip_Select; KBD_AVAIL = Kbd_Available;
  //   CLR = Reset; KBD_CLR = Reset; KBD_DATA[6:0] = Kbd_ASCII_Data; RAM_A[15:0] = Address;
  //   RAM_INPUT_0[31:0] = RAM_In_0; RAM_INPUT_1[31:0] = RAM_In_1; RAM_INPUT_2[31:0] = RAM_In_2;
  //   RAM_INPUT_3[31:0] = RAM_In_3; RAM_MASK[3:0] = Mask; RAM_OUTPUT_0[31:0] = RAM_Out_0;
  //   RAM_OUTPUT_1[31:0] = RAM_Out_1; RAM_OUTPUT_2[31:0] = RAM_Out_2; RAM_OUTPUT_3[31:0] = RAM_Out_3;
  //   RW = nRead_Write; TTY_DATA[6:0] = TTY_ASCII_Data

  // Notes on the sheet:
  //   RAM ADDRESS
  //   DATA FROM RAM
  //   DATA TO RAM
  //   DATA WRITE MASK
  //   RAM TIMING
  //   RAM CONTROL
  //   KEYBOARD
  //   TTY
  //   SEQUENCING
endmodule

module RAM_Dispatcher (
  input  [3:0] WriteTime,
  input  Clock,
  input  CLR,
  output [31:0] Data,
  output [15:0] Address,
  output [3:0] Mask,
  output Finished,
  output Write
);

  wire demultiplexer_2_out1, demultiplexer_3_out1, End, IDLE_q, IncAddr, Load, or_1_out, or_2_out, While_q,
       WriteEnd;
  wire [3:0] counter_1_q;
  wire [31:0] CurrentAddress_q;

  Counter #(.width(32), .max('hffffffff)) CurrentAddress (
    .count(IncAddr), .Q({CurrentAddress_q[31:18], Address, CurrentAddress_q[1:0]}), .clk(Clock), .clr(CLR));  // open: load, D, carry
  or or_1 (or_1_out, IncAddr, demultiplexer_3_out1, Finished);
  D_Flip_Flop IDLE (.clk(Clock), .D(or_1_out), .Q(IDLE_q), .preset(CLR));  // open: Qn, en, reset
  Demultiplexer #(.enable("false")) demultiplexer_1 (.out0(Load), .out1(Finished), .in(IDLE_q), .sel(End));
  D_Flip_Flop While (.clk(Clock), .D(or_2_out), .Q(While_q), .reset(CLR));  // open: Qn, preset, en
  or or_2 (or_2_out, Write, Load);
  RAM_part #(.addrWidth(18), .dataWidth(32)) ram_1 (
    .addr({Address, CurrentAddress_q[1:0]}), .data(Data), .clk(Clock));  // open: sel, ld, clr
  Demultiplexer #(.enable("false")) demultiplexer_2 (
    .out0(Write), .out1(demultiplexer_2_out1), .in(While_q), .sel(WriteEnd));
  Decoder #(.select(2)) decoder_1 (
    .out0(Mask[0]), .out1(Mask[1]), .out2(Mask[2]), .out3(Mask[3]), .sel(CurrentAddress_q[1:0]));  // open: en
  Demultiplexer #(.enable("false")) demultiplexer_3 (
    .out0(IncAddr), .out1(demultiplexer_3_out1), .in(demultiplexer_2_out1), .sel(End));
  Counter #(.width(4), .max('hf)) counter_1 (
    .load(Load), .D(WriteTime), .count(Write), .Q(counter_1_q), .clk(Clock));  // open: carry, clr
  Comparator #(.width(32)) comparator_1 (.a(Data), .b({32{1'b1}}), .eq(End));  // open: gt, lt
  Comparator #(.width(4)) comparator_2 (.a(4'b0000), .b(counter_1_q), .eq(WriteEnd));  // open: gt, lt

  // Other names for the same wires on the sheet: CLK = Clock; Count = Write; WT[3:0] = WriteTime
endmodule

module Data_Path (
  input  Clock,
  input  [1:0] A3Src,
  input  [6:0] Kbd_ASCII_Data,
  input  [2:0] WD3Src,
  input  Reset,
  input  [3:0] ALUControl,
  input  Instru_En,
  input  Result_Load,
  input  ALUSrcA,
  input  [1:0] ALUSrcB,
  input  WriteReg,
  input  Kbd_available,
  input  [1:0] AddressSrc,
  input  PCEnable,
  input  ExtendSrc,
  input  [1:0] BranchSrc,
  input  Value_Src,
  input  [31:0] RamData,
  output [5:0] Op_Code,
  output [5:0] Func_code,
  output [31:0] Address,
  output [31:0] Value,
  output ZF,
  output NF,
  output EQF,
  output [6:0] TTY_DAta
);

  wire [4:0] instruction_decoder_1_output_3, multiplexer_2_out, Rd, Rt;
  wire [15:0] Const;
  wire [25:0] Destino;
  wire [31:0] ALU, alu_1_alu_output, bit_extender_1_out, bit_extender_2_out, bit_extender_3_out,
       branch_control_1_pc_star, Data, Hi, Instruction_q, kbd, Lo, multiplexer_3_out, multiplexer_4_out,
       multiplexer_6_out, multiplexer_7_out, PC, Rand, RT_t, SP;
  wire [31:7] RS;

  Register #(.width(32), .trigger("falling")) Instruction (
    .D(RamData), .en(Instru_En), .Q(Instruction_q), .clk(Clock), .clr(Reset));
  Register #(.width(32)) u_Data (.D(RamData), .en(Clock), .Q(Data), .clk(Clock), .clr(Reset));
  Random #(.width(32)) random_1 (.clk(Clock), .next(Clock), .out(Rand));  // open: clr
  assign bit_extender_1_out = {{25{1'b0}}, Kbd_ASCII_Data};  // Bit_Extender bit_extender_1
  Instruction_Decoder instruction_decoder_1 (
    .Instruction(Instruction_q), .Output(Op_Code), .Output_2(Destino),
    .Output_3(instruction_decoder_1_output_3), .Output_4(Rt), .Output_5(Const), .Output_6(Rd),
    .Output_8(Func_code));  // open: Output_7
  Branch_Control branch_control_1 (
    .PC_star(branch_control_1_pc_star), .RS({RS, TTY_DAta}), .PC(PC), .Destino(Destino), .Offset(Const),
    .BS(BranchSrc));
  Program_Counter program_counter_1 (
    .in_1(branch_control_1_pc_star), .in_2(PCEnable), .in_3(Clock), .in_4(Reset), .Output(PC));
  Multiplexer #(.width(32), .enable("false")) multiplexer_1 (
    .in0({32{1'b1}}), .in1(bit_extender_1_out), .out(kbd), .sel(Kbd_available));
  Register_File register_file_1 (
    .Destination_Adress(multiplexer_2_out), .Data_Input(multiplexer_3_out),
    .Selector_A(instruction_decoder_1_output_3), .Selector_B(Rt), .in_5(Reset), .Read_Write(WriteReg),
    .in_4(Clock), .Output_A({RS, TTY_DAta}), .Output_B(RT_t), .SP(SP));
  Multiplexer #(.select(2), .width(5), .enable("false")) multiplexer_2 (
    .in0(Rd), .in1(Rt), .in2({5{1'b1}}), .out(multiplexer_2_out), .sel(A3Src));  // open: in3
  Multiplexer #(.select(3), .width(32), .enable("false")) multiplexer_3 (
    .in0(ALU), .in1(Data), .in2(Hi), .in3(Lo), .in4(Rand), .in5(kbd), .out(multiplexer_3_out), .sel(WD3Src));  // open: in6, in7
  assign bit_extender_2_out = {{16{Const[15]}}, Const};  // Bit_Extender bit_extender_2
  Multiplexer #(.width(32), .enable("false")) multiplexer_4 (
    .in0(bit_extender_2_out), .in1(bit_extender_3_out), .out(multiplexer_4_out), .sel(ExtendSrc));
  assign bit_extender_3_out = {{16{1'b0}}, Const};  // Bit_Extender bit_extender_3
  Multiplexer #(.select(2), .width(32), .enable("false")) multiplexer_5 (
    .in0(PC), .in1(ALU), .in2(SP), .out(Address), .sel(AddressSrc));  // open: in3
  Multiplexer #(.width(32), .enable("false")) multiplexer_6 (
    .in0({RS, TTY_DAta}), .in1(SP), .out(multiplexer_6_out), .sel(ALUSrcA));
  Multiplexer #(.select(2), .width(32), .enable("false")) multiplexer_7 (
    .in0(RT_t), .in1(32'h4), .in2(multiplexer_4_out), .out(multiplexer_7_out), .sel(ALUSrcB));  // open: in3
  ALU alu_1 (
    .in_1(ALUControl), .in_2(Clock), .in_3(multiplexer_6_out), .in_4(multiplexer_7_out), .HIGH(Hi),
    .ALU_OUTPUT(alu_1_alu_output), .LOW(Lo), .ZF(ZF), .SF(NF), .EQF(EQF));
  Multiplexer #(.width(32), .enable("false")) multiplexer_8 (
    .in0({RS, TTY_DAta}), .in1(RT_t), .out(Value), .sel(Value_Src));
  Register #(.width(32)) ALU_result (.D(alu_1_alu_output), .en(Result_Load), .Q(ALU), .clk(Clock), .clr(Reset));

  // Other names for the same wires on the sheet: AdrSrc[1:0] = AddressSrc; BSrc[1:0] = BranchSrc; CLK = Clock;
  //   Funct[5:0] = Func_code; Instr_en = Instru_En; Op[5:0] = Op_Code; PCEn = PCEnable; RS[6:0] = TTY_DAta;
  //   RST = Reset; ValueSrc = Value_Src; WE3 = WriteReg
endmodule

// tr
module Control_Unit (
  input  in_1,
  input  [3:0] R_Time,
  input  in_3,
  input  [3:0] W_time,
  input  [5:0] in_5,
  input  [5:0] in_6,
  input  in_7,
  input  in_8,
  input  in_9,
  output ALUSrc_A,
  output [1:0] ALUSrc_B,
  output [1:0] Address_Src,
  output Write,
  output [1:0] Branch_Src,
  output CS,
  output [1:0] A3Src,
  output [2:0] WD3Src,
  output [3:0] ALU_Control,
  output WE3,
  output PCEn,
  output TTY_Enable,
  output Stop,
  output Value_Src,
  output Kbd_En,
  output Instr_En,
  output ExtendSrc,
  output Result_Load
);

  wire A3Src_0a, A3Src_0b, A3Src_1a, A3Src_1b, A3Src_1c, AdrSrc_0a, AdrSrc_1a, AdrSrc_1b, ALu_Calc_0a,
       ALu_Calc_0b, ALu_Calc_0c, ALUSrcB_1a, and_1_out, and_2_out, and_3_out, and_4_out, and_5_out,
       and_6_out, and_7_out, and_8_out, and_9_out, Arit, Arit_End, Arit_i, Arit_I_End, comparator_1_gt,
       comparator_2_lt, comparator_3_eq, Copia, Copia_End, CS_a, Decoded, demultiplexer_1_out1,
       demultiplexer_2_out0, demultiplexer_2_out1, demultiplexer_3_out1, demultiplexer_4_out0,
       demultiplexer_4_out1, demultiplexer_6_out0, demultiplexer_6_out1, demultiplexer_8_out0,
       demultiplexer_9_out0, demultiplexer_9_out1, demultiplexer_10_out0, demultiplexer_10_out1,
       demultiplexer_11_out0, demultiplexer_11_out1, Ejecutando_q, Especial, Especial_End, halt, IDLE_q,
       Instr_En_a, Instr_En_b, Lw, lw_End, or_1_out, or_2_out, or_3_out, or_4_out, or_5_out, or_6_out,
       or_7_out, or_9_out, or_11_out, or_12_out, or_13_out, or_15_out, or_20_out, PCEn_c, PCEn_e, PCEn_g,
       Pila, Result_Load_a, rnd, Salto, Salto_End, Sw, timer_1_output, timer_2_output, timer_3_output,
       timer_4_output, timer_5_output, Timer_Reset, WD3Src_0a, WD3Src_0d, WE3_a;
  wire [1:0] ALU_Calc;
  wire [3:0] ALU_S;

  or or_1 (or_1_out, or_13_out, demultiplexer_3_out1);
  and and_1 (and_1_out, Decoded, Copia);
  D_Flip_Flop #(.trigger("falling")) IDLE (.clk(in_1), .D(or_1_out), .Q(IDLE_q), .preset(in_3));  // open: Qn, en, reset
  Comparator #(.width(6)) comparator_1 (.a(in_6), .b(6'b010011), .gt(comparator_1_gt));  // open: eq, lt
  Comparator #(.width(6)) comparator_2 (.a(in_6), .b(6'b011100), .lt(comparator_2_lt));  // open: gt, eq
  D_Flip_Flop #(.trigger("falling")) Calculando (
    .clk(in_1), .D(and_2_out), .Q(Result_Load_a), .reset(in_3));  // open: Qn, preset, en
  and and_2 (and_2_out, Decoded, Arit);
  Comparator #(.width(6)) comparator_3 (.a(in_6), .b(6'b010000), .eq(comparator_3_eq));  // open: gt, lt
  D_Flip_Flop #(.trigger("falling")) Copiando (
    .clk(in_1), .D(and_1_out), .Q(WD3Src[1]), .reset(in_3));  // open: Qn, preset, en
  Demultiplexer #(.enable("false")) demultiplexer_1 (
    .out0(WD3Src_0a), .out1(demultiplexer_1_out1), .in(WD3Src[1]), .sel(comparator_3_eq));
  D_Flip_Flop #(.trigger("falling")) Saltando (
    .clk(in_1), .D(and_3_out), .Q(PCEn_c), .reset(in_3));  // open: Qn, preset, en
  and and_3 (and_3_out, Decoded, Salto);
  D_Flip_Flop #(.trigger("falling")) Calculando_2 (
    .clk(in_1), .D(and_4_out), .Q(ALUSrcB_1a), .reset(in_3));  // open: Qn, preset, en
  and and_4 (and_4_out, Decoded, Arit_i);
  Demultiplexer #(.enable("false")) demultiplexer_2 (
    .out0(demultiplexer_2_out0), .out1(demultiplexer_2_out1), .in(and_5_out), .sel(in_6[0]));
  and and_5 (and_5_out, Decoded, Pila);
  D_Flip_Flop #(.trigger("falling")) Calculando_3 (
    .clk(in_1), .D(and_6_out), .Q(ALu_Calc_0b), .reset(in_3));  // open: Qn, preset, en
  and and_6 (and_6_out, Decoded, Lw);
  D_Flip_Flop #(.trigger("falling")) Calculando_4 (
    .clk(in_1), .D(and_7_out), .Q(ALu_Calc_0c), .reset(in_3));  // open: Qn, preset, en
  and and_7 (and_7_out, Decoded, Sw);
  D_Flip_Flop #(.trigger("falling")) Ejecutando (
    .clk(in_1), .D(and_8_out), .Q(Ejecutando_q), .reset(in_3));  // open: Qn, preset, en
  and and_8 (and_8_out, Decoded, Especial);
  Demultiplexer #(.enable("false")) demultiplexer_3 (
    .out0(Timer_Reset), .out1(demultiplexer_3_out1), .in(IDLE_q), .sel(in_3));
  and and_9 (and_9_out, comparator_1_gt, comparator_2_lt);
  Demultiplexer #(.enable("false")) demultiplexer_4 (
    .out0(demultiplexer_4_out0), .out1(demultiplexer_4_out1), .in(Result_Load_a), .sel(and_9_out));
  or or_2 (or_2_out, demultiplexer_6_out0, demultiplexer_2_out0);
  Demultiplexer #(.select(2), .enable("false")) demultiplexer_5 (
    .out0(TTY_Enable), .out1(rnd), .out2(Kbd_En), .out3(halt), .in(Ejecutando_q), .sel(in_6[2:1]));
  D_Flip_Flop #(.trigger("falling")) u_Salto_End (
    .clk(in_1), .D(PCEn_c), .Q(Salto_End), .reset(in_3));  // open: Qn, preset, en
  D_Flip_Flop #(.trigger("falling")) Write_Reg (
    .clk(in_1), .D(ALUSrcB_1a), .Q(A3Src_0a), .reset(in_3));  // open: Qn, preset, en
  D_Flip_Flop #(.trigger("falling")) Read_Ram (
    .clk(in_1), .D(or_2_out), .Q(AdrSrc_1a), .reset(in_3));  // open: Qn, preset, en
  D_Flip_Flop #(.trigger("falling")) Update_POinter (
    .clk(in_1), .D(demultiplexer_2_out1), .Q(ALU_Calc[1]), .reset(in_3));  // open: Qn, preset, en
  or or_3 (or_3_out, demultiplexer_10_out0, ALu_Calc_0c);
  or or_4 (or_4_out, Instr_En_b, Timer_Reset);
  D_Flip_Flop #(.trigger("falling")) Write_Reg_2 (
    .clk(in_1), .D(demultiplexer_4_out0), .Q(WE3_a), .reset(in_3));  // open: Qn, preset, en
  D_Flip_Flop #(.trigger("falling")) u_Copia_End (
    .clk(in_1), .D(or_5_out), .Q(Copia_End), .reset(in_3));  // open: Qn, preset, en
  or or_5 (or_5_out, WD3Src_0a, demultiplexer_1_out1);
  Timer timer_1 (.in_1(R_Time), .in_2(in_1), .Output(timer_1_output), .in_3(in_1), .in_4(Timer_Reset));
  D_Flip_Flop #(.trigger("falling")) Read_Ram_2 (
    .clk(in_1), .D(or_6_out), .Q(AdrSrc_0a), .reset(in_3));  // open: Qn, preset, en
  or or_6 (or_6_out, demultiplexer_9_out0, ALu_Calc_0b);
  D_Flip_Flop #(.trigger("falling")) u_Write (
    .clk(in_1), .D(or_3_out), .Q(Value_Src), .reset(in_3));  // open: Qn, preset, en
  D_Flip_Flop #(.trigger("falling")) Fetch_Instr (
    .clk(in_1), .D(or_4_out), .Q(CS_a), .reset(in_3));  // open: Qn, preset, en
  or or_7 (or_7_out, WE3_a, demultiplexer_4_out1);
  Demultiplexer #(.enable("false")) demultiplexer_6 (
    .out0(demultiplexer_6_out0), .out1(demultiplexer_6_out1), .in(AdrSrc_1a), .sel(timer_1_output));
  or or_8 (WD3Src[2], rnd, Kbd_En);
  or or_9 (or_9_out, Stop, halt);
  Demultiplexer #(.enable("false")) demultiplexer_7 (
    .out0(Instr_En_b), .out1(Instr_En_a), .in(CS_a), .sel(timer_2_output));
  Timer timer_2 (.in_1(R_Time), .in_2(in_1), .Output(timer_2_output), .in_3(in_1), .in_4(Timer_Reset));
  D_Flip_Flop #(.trigger("falling")) u_Arit_End (
    .clk(in_1), .D(or_7_out), .Q(Arit_End), .reset(in_3));  // open: Qn, preset, en
  D_Flip_Flop #(.trigger("falling")) Tipo_I_End (
    .clk(in_1), .D(A3Src_0a), .Q(Arit_I_End), .reset(in_3));  // open: Qn, preset, en
  D_Flip_Flop #(.trigger("falling")) Write_Reg_3 (
    .clk(in_1), .D(ALU_Calc[1]), .Q(A3Src_1b), .reset(in_3));  // open: Qn, preset, en
  Timer timer_3 (.in_1(R_Time), .in_2(in_1), .Output(timer_3_output), .in_3(in_1), .in_4(Timer_Reset));
  Timer timer_4 (.in_1(W_time), .in_2(in_1), .Output(timer_4_output), .in_3(in_1), .in_4(Timer_Reset));
  Demultiplexer #(.enable("false")) demultiplexer_8 (
    .out0(demultiplexer_8_out0), .out1(WD3Src_0d), .in(WD3Src[2]), .sel(Kbd_En));
  D_Flip_Flop #(.trigger("falling")) Programa_Terminado (
    .clk(in_1), .D(or_9_out), .Q(Stop), .reset(in_3));  // open: Qn, preset, en
  Operation_Decoder operation_decoder_1 (
    .OpCode(in_5), .Function(in_6), .ZF(in_7), .NF(in_8), .EQF(in_9), .ALUControl(ALU_S), .Arit_I(Arit_i),
    .BCSrc(Branch_Src), .Arit(Arit), .Copia(Copia), .Pila(Pila), .Salto(Salto), .Especial(Especial),
    .Load_Word(Lw), .Store_Word(Sw), .ExtendSrc(ExtendSrc));
  D_Flip_Flop #(.trigger("falling")) u_Decoded (
    .clk(in_1), .D(Instr_En_a), .Q(Decoded), .reset(in_3));  // open: Qn, preset, en
  D_Flip_Flop #(.trigger("falling")) Write_Reg_4 (
    .clk(in_1), .D(demultiplexer_6_out1), .Q(A3Src_1c), .reset(in_3));  // open: Qn, preset, en
  Demultiplexer #(.enable("false")) demultiplexer_9 (
    .out0(demultiplexer_9_out0), .out1(demultiplexer_9_out1), .in(AdrSrc_0a), .sel(timer_3_output));
  Demultiplexer #(.enable("false")) demultiplexer_10 (
    .out0(demultiplexer_10_out0), .out1(demultiplexer_10_out1), .in(Value_Src), .sel(timer_4_output));
  or or_10 (Instr_En, Instr_En_a, Instr_En_b);
  D_Flip_Flop #(.trigger("falling")) Write_Reg_5 (
    .clk(in_1), .D(demultiplexer_9_out1), .Q(A3Src_0b), .reset(in_3));  // open: Qn, preset, en
  D_Flip_Flop #(.trigger("falling")) Sw_End (
    .clk(in_1), .D(demultiplexer_10_out1), .Q(PCEn_g), .reset(in_3));  // open: Qn, preset, en
  or or_11 (or_11_out, demultiplexer_8_out0, WD3Src_0d);
  or or_12 (or_12_out, or_11_out, TTY_Enable);
  or or_13 (or_13_out, Arit_End, Copia_End, PCEn_e, Salto_End, Arit_I_End, Especial_End, lw_End, PCEn_g);
  D_Flip_Flop #(.trigger("falling")) Update_POinter_2 (
    .clk(in_1), .D(A3Src_1c), .Q(ALu_Calc_0a), .reset(in_3));  // open: Qn, preset, en
  D_Flip_Flop #(.trigger("falling")) u_Especial_End (
    .clk(in_1), .D(or_12_out), .Q(Especial_End), .reset(in_3));  // open: Qn, preset, en
  or or_14 (Result_Load, Result_Load_a, ALUSrcB_1a, ALu_Calc_0a, ALU_Calc[1], ALu_Calc_0b, ALu_Calc_0c);
  or or_15 (or_15_out, demultiplexer_11_out0, A3Src_1b);
  D_Flip_Flop #(.trigger("falling")) Write_2 (
    .clk(in_1), .D(or_15_out), .Q(AdrSrc_1b), .reset(in_3));  // open: Qn, preset, en
  D_Flip_Flop #(.trigger("falling")) u_Lw_End (
    .clk(in_1), .D(A3Src_0b), .Q(lw_End), .reset(in_3));  // open: Qn, preset, en
  D_Flip_Flop #(.trigger("falling")) Write_Reg_6 (
    .clk(in_1), .D(ALu_Calc_0a), .Q(A3Src_1a), .reset(in_3));  // open: Qn, preset, en
  or or_16 (PCEn, Arit_End, Copia_End, PCEn_c, Arit_I_End, PCEn_e, lw_End, PCEn_g, Especial_End);
  or or_17 (WE3, WE3_a, A3Src_0a, A3Src_1a, A3Src_1b, A3Src_0b, WD3Src[2], A3Src_1c, WD3Src[1]);
  or or_18 (A3Src[1], A3Src_1a, A3Src_1b, A3Src_1c);
  or or_19 (A3Src[0], A3Src_0a, A3Src_0b);
  Timer timer_5 (.in_1(W_time), .in_2(in_1), .Output(timer_5_output), .in_3(in_1), .in_4(Timer_Reset));
  Demultiplexer #(.enable("false")) demultiplexer_11 (
    .out0(demultiplexer_11_out0), .out1(demultiplexer_11_out1), .in(AdrSrc_1b), .sel(timer_5_output));
  D_Flip_Flop #(.trigger("falling")) Pila_End (
    .clk(in_1), .D(or_20_out), .Q(PCEn_e), .reset(in_3));  // open: Qn, preset, en
  or or_20 (or_20_out, A3Src_1a, demultiplexer_11_out1);
  or or_21 (CS, CS_a, AdrSrc_1a, AdrSrc_1b, AdrSrc_0a, Value_Src);
  or or_22 (ALUSrc_A, ALu_Calc_0a, ALU_Calc[1]);
  Multiplexer #(.select(2), .width(4), .enable("false")) multiplexer_1 (
    .in0(ALU_S), .in1(4'b0110), .in2(4'b0111), .out(ALU_Control), .sel(ALU_Calc));  // open: in3
  or or_23 (Address_Src[1], AdrSrc_1a, AdrSrc_1b);
  or or_24 (Write, AdrSrc_1b, Value_Src);
  or or_25 (WD3Src[0], WD3Src_0a, A3Src_1c, A3Src_0b, WD3Src_0d);
  or or_26 (ALUSrc_B[0], ALu_Calc_0a, ALU_Calc[1]);
  or or_27 (ALU_Calc[0], ALu_Calc_0a, ALu_Calc_0b, ALu_Calc_0c);
  or or_28 (Address_Src[0], AdrSrc_0a, Value_Src);
  or or_29 (ALUSrc_B[1], ALUSrcB_1a, ALu_Calc_0b, ALu_Calc_0c);

  // Other names for the same wires on the sheet: A3Src_0 = A3Src[0]; A3Src_1 = A3Src[1]; AdrSrc[1:0] = Address_Src;
  //   AdrSrc_0 = Address_Src[0]; AdrSrc_1 = Address_Src[1]; ALU_Calc_0 = ALU_Calc[0]; ALu_Calc_1 = ALU_Calc[1];
  //   ALUSrcA_b = ALU_Calc[1]; ALUSrcB_0b = ALU_Calc[1]; Result_Load_d = ALU_Calc[1]; ALUControl[3:0] = ALU_Control;
  //   ALUSrcA = ALUSrc_A; ALUSrcB[1:0] = ALUSrc_B; ALUSrcB_0 = ALUSrc_B[0]; ALUSrcB_1 = ALUSrc_B[1];
  //   BSrc[1:0] = Branch_Src; CLK = in_1; CS_b = AdrSrc_1a; CS_d = AdrSrc_0a; EQF = in_9; Func_Code[5:0] = in_6;
  //   kbd = Kbd_En; PCEn_f = lw_End; NF = in_8; Op_Code[5:0] = in_5; PCEn_a = Arit_End; PCEn_b = Copia_End;
  //   PCEn_d = Arit_I_End; PCEn_h = Especial_End; Pila_End = PCEn_e; Reset = in_3; Result_Load_b = ALUSrcB_1a;
  //   ALUSrcA_a = ALu_Calc_0a; ALUSrcB_0a = ALu_Calc_0a; Result_Load_c = ALu_Calc_0a; ALUSrcB_1b = ALu_Calc_0b;
  //   Result_Load_e = ALu_Calc_0b; ALUSrcB_1c = ALu_Calc_0c; Result_Load_f = ALu_Calc_0c; Sw_End = PCEn_g;
  //   tty = TTY_Enable; WD3Src_0 = WD3Src[0]; WD3Src_1a = WD3Src[1]; WE3_h = WD3Src[1]; WD3Src_2 = WD3Src[2];
  //   WE3_f = WD3Src[2]; WE3_b = A3Src_0a; WE3_c = A3Src_1a; WE3_d = A3Src_1b; WD3Src_0c = A3Src_0b; WE3_e = A3Src_0b;
  //   WD3Src_0b = A3Src_1c; WE3_g = A3Src_1c; CS_c = AdrSrc_1b; Write_a = AdrSrc_1b; AdrSrc_0b = Value_Src;
  //   CS_e = Value_Src; Write_b = Value_Src; ZF = in_7

  // Notes on the sheet:
  //   ASM Aritmetica
  //   ASM Copia
  //   ASM Salto
  //   ASM Aritmetica Tipo I
  //   ASM Pila
  //   ASM Especial
  //   ASM Lw
  //   ASM Sw
endmodule

module Operation_Decoder (
  input  [5:0] OpCode,
  input  [5:0] Function,
  input  ZF,
  input  NF,
  input  EQF,
  output [3:0] ALUControl,
  output ExtendSrc,
  output [1:0] BCSrc,
  output Arit,
  output Copia,
  output Pila,
  output Salto,
  output Arit_I,
  output Especial,
  output Load_Word,
  output Store_Word
);

  wire add, addi, \and , and_1_out, and_2_out, and_15_out, and_16_out, and_17_out, and_18_out, and_19_out,
       andi, beq, bgtz, blez, bltz, bne, comparator_3_lt, comparator_4_eq, comparator_4_gt, comparator_5_lt,
       comparator_6_gt, comparator_7_lt, comparator_8_gt, comparator_9_eq, comparator_10_eq,
       comparator_11_eq, comparator_12_eq, comparator_13_eq, comparator_14_eq, comparator_15_eq,
       comparator_16_eq, comparator_17_eq, comparator_18_eq, comparator_19_eq, comparator_20_eq,
       comparator_21_eq, comparator_22_eq, comparator_23_eq, comparator_24_eq, comparator_25_eq,
       comparator_26_eq, comparator_27_eq, comparator_28_eq, comparator_29_eq, comparator_30_eq,
       comparator_32_eq, comparator_33_eq, comparator_34_eq, div, divu, halt, j, jr, kbd, mfhi, mflo, mult,
       mulu, nop, \nor , \or , or_3_out, ori, pop, push, rnd, RS__0_t, RS___0, RS____RT, slt, stli, stliu,
       stlu, sub, tty, \xor , xori;

  or or_1 (RS___0, ZF, NF);
  not not_1 (RS____RT, EQF);
  Comparator #(.width(6), .mode("unsigned")) comparator_1 (.a(OpCode), .b({6{1'b1}}), .eq(Especial));  // open: gt, lt
  Comparator #(.width(6), .mode("unsigned")) comparator_2 (.a(OpCode), .b(6'b111000), .eq(Pila));  // open: gt, lt
  Comparator #(.width(6), .mode("unsigned")) comparator_3 (
    .a(OpCode), .b(6'b001000), .lt(comparator_3_lt));  // open: gt, eq
  Comparator #(.width(6), .mode("unsigned")) comparator_4 (
    .a(OpCode), .b({6{1'b0}}), .gt(comparator_4_gt), .eq(comparator_4_eq));  // open: lt
  Comparator #(.width(6), .mode("unsigned")) comparator_5 (
    .a(Function), .b(6'b001001), .lt(comparator_5_lt));  // open: gt, eq
  Comparator #(.width(6), .mode("unsigned")) comparator_6 (
    .a(Function), .b(6'b001111), .gt(comparator_6_gt));  // open: eq, lt
  Comparator #(.width(6), .mode("unsigned")) comparator_7 (
    .a(Function), .b(6'b010011), .lt(comparator_7_lt));  // open: gt, eq
  Comparator #(.width(6), .mode("unsigned")) comparator_8 (
    .a(Function), .b(6'b010111), .gt(comparator_8_gt));  // open: eq, lt
  not not_2 (RS__0_t, RS___0);
  and and_1 (and_1_out, comparator_3_lt, comparator_4_gt);
  and and_2 (and_2_out, comparator_4_eq, comparator_5_lt);
  and and_3 (Copia, comparator_4_eq, comparator_6_gt, comparator_7_lt);
  and and_4 (Arit, comparator_4_eq, comparator_8_gt);
  or or_2 (Salto, and_1_out, and_2_out);
  Comparator #(.width(6)) comparator_9 (.a(OpCode), .b({6{1'b0}}), .eq(comparator_9_eq));  // open: gt, lt
  Comparator #(.width(6)) comparator_10 (.a(Function), .b(6'b100000), .eq(comparator_10_eq));  // open: gt, lt
  Comparator #(.width(6)) comparator_11 (.a(Function), .b(6'b100010), .eq(comparator_11_eq));  // open: gt, lt
  Comparator #(.width(6)) comparator_12 (.a(Function), .b(6'b011000), .eq(comparator_12_eq));  // open: gt, lt
  Comparator #(.width(6)) comparator_13 (.a(Function), .b(6'b011001), .eq(comparator_13_eq));  // open: gt, lt
  Comparator #(.width(6)) comparator_14 (.a(Function), .b(6'b011010), .eq(comparator_14_eq));  // open: gt, lt
  Comparator #(.width(6)) comparator_15 (.a(Function), .b(6'b011011), .eq(comparator_15_eq));  // open: gt, lt
  Comparator #(.width(6)) comparator_16 (.a(Function), .b(6'b100100), .eq(comparator_16_eq));  // open: gt, lt
  Comparator #(.width(6)) comparator_17 (.a(Function), .b(6'b100101), .eq(comparator_17_eq));  // open: gt, lt
  Comparator #(.width(6)) comparator_18 (.a(Function), .b(6'b100111), .eq(comparator_18_eq));  // open: gt, lt
  Comparator #(.width(6)) comparator_19 (.a(Function), .b(6'b101000), .eq(comparator_19_eq));  // open: gt, lt
  and and_5 (add, comparator_9_eq, comparator_10_eq);
  and and_6 (sub, comparator_9_eq, comparator_11_eq);
  and and_7 (mult, comparator_9_eq, comparator_12_eq);
  and and_8 (mulu, comparator_9_eq, comparator_13_eq);
  and and_9 (div, comparator_9_eq, comparator_14_eq);
  and and_10 (divu, comparator_9_eq, comparator_15_eq);
  and and_11 (\and , comparator_9_eq, comparator_16_eq);
  and and_12 (\or , comparator_9_eq, comparator_17_eq);
  and and_13 (\nor , comparator_9_eq, comparator_18_eq);
  and and_14 (\xor , comparator_9_eq, comparator_19_eq);
  and and_15 (and_15_out, beq, EQF);
  and and_16 (and_16_out, bne, RS____RT);
  and and_17 (and_17_out, blez, RS___0);
  and and_18 (and_18_out, bgtz, RS__0_t);
  and and_19 (and_19_out, bltz, NF);
  or or_3 (or_3_out, and_15_out, and_16_out, and_17_out, and_18_out, and_19_out);
  or or_4 (BCSrc[0], or_3_out, jr);
  or or_5 (BCSrc[1], jr, j);
  and and_20 (slt, comparator_9_eq, comparator_20_eq);
  Comparator #(.width(6)) comparator_20 (.a(Function), .b(6'b101010), .eq(comparator_20_eq));  // open: gt, lt
  and and_21 (stlu, comparator_9_eq, comparator_21_eq);
  Comparator #(.width(6)) comparator_21 (.a(Function), .b(6'b101011), .eq(comparator_21_eq));  // open: gt, lt
  and and_22 (mfhi, comparator_9_eq, comparator_22_eq);
  Comparator #(.width(6)) comparator_22 (.a(Function), .b(6'b010000), .eq(comparator_22_eq));  // open: gt, lt
  and and_23 (mflo, comparator_9_eq, comparator_23_eq);
  Comparator #(.width(6)) comparator_23 (.a(Function), .b(6'b010010), .eq(comparator_23_eq));  // open: gt, lt
  and and_24 (nop, comparator_9_eq, comparator_24_eq);
  Comparator #(.width(6)) comparator_24 (.a(Function), .b({6{1'b0}}), .eq(comparator_24_eq));  // open: gt, lt
  and and_25 (jr, comparator_9_eq, comparator_25_eq);
  Comparator #(.width(6)) comparator_25 (.a(Function), .b(6'b001000), .eq(comparator_25_eq));  // open: gt, lt
  Comparator #(.width(6)) comparator_26 (.a(OpCode), .b({6{1'b1}}), .eq(comparator_26_eq));  // open: gt, lt
  Comparator #(.width(6)) comparator_27 (.a(Function), .b({6{1'b1}}), .eq(comparator_27_eq));  // open: gt, lt
  Comparator #(.width(6)) comparator_28 (.a(Function), .b(6'b000001), .eq(comparator_28_eq));  // open: gt, lt
  Comparator #(.width(6)) comparator_29 (.a(Function), .b(6'b000010), .eq(comparator_29_eq));  // open: gt, lt
  Comparator #(.width(6)) comparator_30 (.a(Function), .b(6'b000100), .eq(comparator_30_eq));  // open: gt, lt
  or or_6 (ExtendSrc, andi, ori, xori);
  and and_26 (halt, comparator_26_eq, comparator_27_eq);
  and and_27 (tty, comparator_26_eq, comparator_28_eq);
  and and_28 (rnd, comparator_26_eq, comparator_29_eq);
  and and_29 (kbd, comparator_26_eq, comparator_30_eq);
  Comparator #(.width(6)) comparator_31 (.a(OpCode), .b(6'b000010), .eq(j));  // open: gt, lt
  Comparator #(.width(6)) comparator_32 (.a(OpCode), .b(6'b111000), .eq(comparator_32_eq));  // open: gt, lt
  Comparator #(.width(6)) comparator_33 (.a(Function), .b({6{1'b0}}), .eq(comparator_33_eq));  // open: gt, lt
  Comparator #(.width(6)) comparator_34 (.a(Function), .b(6'b000001), .eq(comparator_34_eq));  // open: gt, lt
  and and_30 (pop, comparator_32_eq, comparator_33_eq);
  and and_31 (push, comparator_32_eq, comparator_34_eq);
  Comparator #(.width(6)) comparator_35 (.a(OpCode), .b(6'b001000), .eq(addi));  // open: gt, lt
  Comparator #(.width(6)) comparator_36 (.a(OpCode), .b(6'b001100), .eq(andi));  // open: gt, lt
  Comparator #(.width(6)) comparator_37 (.a(OpCode), .b(6'b001101), .eq(ori));  // open: gt, lt
  Comparator #(.width(6)) comparator_38 (.a(OpCode), .b(6'b001110), .eq(xori));  // open: gt, lt
  Comparator #(.width(6)) comparator_39 (.a(OpCode), .b(6'b100011), .eq(Load_Word));  // open: gt, lt
  Comparator #(.width(6)) comparator_40 (.a(OpCode), .b(6'b101011), .eq(Store_Word));  // open: gt, lt
  ALU_Encoder alu_encoder_1 (
    .ADD(add), .ADDI(addi), .SUB(sub), .MULT(mult), .MULU(mulu), .DIV(div), .DIVU(divu), .SLT(slt),
    .SLTI(stli), .SLTU(stlu), .SLTIU(stliu), .AND(\and ), .ANDI(andi), .OR(\or ), .ORI(ori), .XOR(\xor ),
    .XORI(xori), .NOR(\nor ), .Type_I(Arit_I), .ALU_SELECTOR(ALUControl));
  Comparator #(.width(6)) comparator_41 (.a(OpCode), .b(6'b001010), .eq(stli));  // open: gt, lt
  Comparator #(.width(6)) comparator_42 (.a(OpCode), .b(6'b001011), .eq(stliu));  // open: gt, lt
  Comparator #(.width(6)) comparator_43 (.a(OpCode), .b(6'b000100), .eq(beq));  // open: gt, lt
  Comparator #(.width(6)) comparator_44 (.a(OpCode), .b(6'b000101), .eq(bne));  // open: gt, lt
  Comparator #(.width(6)) comparator_45 (.a(OpCode), .b(6'b000110), .eq(blez));  // open: gt, lt
  Comparator #(.width(6)) comparator_46 (.a(OpCode), .b(6'b000111), .eq(bgtz));  // open: gt, lt
  Comparator #(.width(6)) comparator_47 (.a(OpCode), .b(6'b000001), .eq(bltz));  // open: gt, lt

  // Other names for the same wires on the sheet: Aritmetica = Arit; Func_code[5:0] = Function; lw = Load_Word;
  //   RS__0 = NF; RS____RT_t = EQF; sw = Store_Word

  // Notes on the sheet:
  //   Instrucciones Tipo R:
  //   Aritmeticas
  //   Logicas
  //   Comparacion
  //   Copia de Registros
  //   Salto
  //   Especiales
  //   Instrucciones Tipo J:
  //   Salto
  //   Memoria
  //   Instrucciones Tipo I:
  //   Aritmeticas
  //   Logicas
  //   Memoria
  //   Comparacion
  //   Salto
endmodule

module Program_Counter (
  input  [31:0] in_1,
  input  in_2,
  input  in_3,
  input  in_4,
  output [31:0] Output
);

  Register #(.width(32)) register_1 (.D(in_1), .en(in_2), .Q(Output), .clk(in_3), .clr(in_4));
endmodule

module Register_File (
  input  [4:0] Destination_Adress,
  input  Read_Write,
  input  [31:0] Data_Input,
  input  in_4,
  input  in_5,
  input  [4:0] Selector_A,
  input  [4:0] Selector_B,
  output [31:0] Output_A,
  output [31:0] Output_B,
  output [31:0] SP
);

  wire Input_00, Input_01, Input_02, Input_03, Input_04, Input_05, Input_06, Input_07, Input_08, Input_09,
       Input_10, Input_11, Input_12, Input_13, Input_14, Input_15, Input_16, Input_17, Input_18, Input_19,
       Input_20, Input_21, Input_22, Input_23, Input_24, Input_25, Input_26, Input_27, Input_28, Input_29,
       Input_30, Input_31;
  wire [31:0] Registro_00, Registro_01, Registro_02, Registro_03, Registro_04, Registro_05, Registro_06,
       Registro_07, Registro_08, Registro_09, Registro_10, Registro_11, Registro_12, Registro_13,
       Registro_14, Registro_15, Registro_16, Registro_17, Registro_18, Registro_19, Registro_20,
       Registro_21, Registro_22, Registro_23, Registro_24, Registro_25, Registro_26, Registro_27,
       Registro_28, Registro_29, Registro_30;

  Demultiplexer #(.select(5)) demultiplexer_1 (
    .out0(Input_00), .out1(Input_01), .out2(Input_02), .out3(Input_03), .out4(Input_04), .out5(Input_05),
    .out6(Input_06), .out7(Input_07), .out8(Input_08), .out9(Input_09), .out10(Input_10), .out11(Input_11),
    .out12(Input_12), .out13(Input_13), .out14(Input_14), .out15(Input_15), .out16(Input_16),
    .out17(Input_17), .out18(Input_18), .out19(Input_19), .out20(Input_20), .out21(Input_21),
    .out22(Input_22), .out23(Input_23), .out24(Input_24), .out25(Input_25), .out26(Input_26),
    .out27(Input_27), .out28(Input_28), .out29(Input_29), .out30(Input_30), .out31(Input_31),
    .in(Read_Write), .sel(Destination_Adress));  // open: en
  Multiplexer #(.select(5), .width(32), .enable("false")) multiplexer_1 (
    .in0(Registro_00), .in1(Registro_01), .in2(Registro_02), .in3(Registro_03), .in4(Registro_04),
    .in5(Registro_05), .in6(Registro_06), .in7(Registro_07), .in8(Registro_08), .in9(Registro_09),
    .in10(Registro_10), .in11(Registro_11), .in12(Registro_12), .in13(Registro_13), .in14(Registro_14),
    .in15(Registro_15), .in16(Registro_16), .in17(Registro_17), .in18(Registro_18), .in19(Registro_19),
    .in20(Registro_20), .in21(Registro_21), .in22(Registro_22), .in23(Registro_23), .in24(Registro_24),
    .in25(Registro_25), .in26(Registro_26), .in27(Registro_27), .in28(Registro_28), .in29(Registro_29),
    .in30(Registro_30), .in31(SP), .out(Output_A), .sel(Selector_A));
  Register #(.width(32)) u_Registro_00 (.D({32{1'b0}}), .en(Input_00), .Q(Registro_00), .clk(in_4), .clr(in_5));
  Register #(.width(32)) u_Registro_01 (.D(Data_Input), .en(Input_01), .Q(Registro_01), .clk(in_4), .clr(in_5));
  Register #(.width(32)) u_Registro_02 (.D(Data_Input), .en(Input_02), .Q(Registro_02), .clk(in_4), .clr(in_5));
  Register #(.width(32)) u_Registro_03 (.D(Data_Input), .en(Input_03), .Q(Registro_03), .clk(in_4), .clr(in_5));
  Register #(.width(32)) u_Registro_04 (.D(Data_Input), .en(Input_04), .Q(Registro_04), .clk(in_4), .clr(in_5));
  Register #(.width(32)) u_Registro_05 (.D(Data_Input), .en(Input_05), .Q(Registro_05), .clk(in_4), .clr(in_5));
  Register #(.width(32)) u_Registro_06 (.D(Data_Input), .en(Input_06), .Q(Registro_06), .clk(in_4), .clr(in_5));
  Register #(.width(32)) u_Registro_07 (.D(Data_Input), .en(Input_07), .Q(Registro_07), .clk(in_4), .clr(in_5));
  Multiplexer #(.select(5), .width(32), .enable("false")) multiplexer_2 (
    .in0(Registro_00), .in1(Registro_01), .in2(Registro_02), .in3(Registro_03), .in4(Registro_04),
    .in5(Registro_05), .in6(Registro_06), .in7(Registro_07), .in8(Registro_08), .in9(Registro_09),
    .in10(Registro_10), .in11(Registro_11), .in12(Registro_12), .in13(Registro_13), .in14(Registro_14),
    .in15(Registro_15), .in16(Registro_16), .in17(Registro_17), .in18(Registro_18), .in19(Registro_19),
    .in20(Registro_20), .in21(Registro_21), .in22(Registro_22), .in23(Registro_23), .in24(Registro_24),
    .in25(Registro_25), .in26(Registro_26), .in27(Registro_27), .in28(Registro_28), .in29(Registro_29),
    .in30(Registro_30), .in31(SP), .out(Output_B), .sel(Selector_B));
  Register #(.width(32)) u_Registro_08 (.D(Data_Input), .en(Input_08), .Q(Registro_08), .clk(in_4), .clr(in_5));
  Register #(.width(32)) u_Registro_09 (.D(Data_Input), .en(Input_09), .Q(Registro_09), .clk(in_4), .clr(in_5));
  Register #(.width(32)) u_Registro_10 (.D(Data_Input), .en(Input_10), .Q(Registro_10), .clk(in_4), .clr(in_5));
  Register #(.width(32)) u_Registro_11 (.D(Data_Input), .en(Input_11), .Q(Registro_11), .clk(in_4), .clr(in_5));
  Register #(.width(32)) u_Registro_12 (.D(Data_Input), .en(Input_12), .Q(Registro_12), .clk(in_4), .clr(in_5));
  Register #(.width(32)) u_Registro_13 (.D(Data_Input), .en(Input_13), .Q(Registro_13), .clk(in_4), .clr(in_5));
  Register #(.width(32)) u_Registro_14 (.D(Data_Input), .en(Input_14), .Q(Registro_14), .clk(in_4), .clr(in_5));
  Register #(.width(32)) u_Registro_15 (.D(Data_Input), .en(Input_15), .Q(Registro_15), .clk(in_4), .clr(in_5));
  Register #(.width(32)) u_Registro_16 (.D(Data_Input), .en(Input_16), .Q(Registro_16), .clk(in_4), .clr(in_5));
  Register #(.width(32)) u_Registro_17 (.D(Data_Input), .en(Input_17), .Q(Registro_17), .clk(in_4), .clr(in_5));
  Register #(.width(32)) u_Registro_18 (.D(Data_Input), .en(Input_18), .Q(Registro_18), .clk(in_4), .clr(in_5));
  Register #(.width(32)) u_Registro_19 (.D(Data_Input), .en(Input_19), .Q(Registro_19), .clk(in_4), .clr(in_5));
  Register #(.width(32)) u_Registro_20 (.D(Data_Input), .en(Input_20), .Q(Registro_20), .clk(in_4), .clr(in_5));
  Register #(.width(32)) u_Registro_21 (.D(Data_Input), .en(Input_21), .Q(Registro_21), .clk(in_4), .clr(in_5));
  Register #(.width(32)) u_Registro_22 (.D(Data_Input), .en(Input_22), .Q(Registro_22), .clk(in_4), .clr(in_5));
  Register #(.width(32)) u_Registro_23 (.D(Data_Input), .en(Input_23), .Q(Registro_23), .clk(in_4), .clr(in_5));
  Register #(.width(32)) u_Registro_24 (.D(Data_Input), .en(Input_24), .Q(Registro_24), .clk(in_4), .clr(in_5));
  Register #(.width(32)) u_Registro_25 (.D(Data_Input), .en(Input_25), .Q(Registro_25), .clk(in_4), .clr(in_5));
  Register #(.width(32)) u_Registro_26 (.D(Data_Input), .en(Input_26), .Q(Registro_26), .clk(in_4), .clr(in_5));
  Register #(.width(32)) u_Registro_27 (.D(Data_Input), .en(Input_27), .Q(Registro_27), .clk(in_4), .clr(in_5));
  Register #(.width(32)) u_Registro_28 (.D(Data_Input), .en(Input_28), .Q(Registro_28), .clk(in_4), .clr(in_5));
  Register #(.width(32)) u_Registro_29 (.D(Data_Input), .en(Input_29), .Q(Registro_29), .clk(in_4), .clr(in_5));
  Register #(.width(32)) u_Registro_30 (.D(Data_Input), .en(Input_30), .Q(Registro_30), .clk(in_4), .clr(in_5));
  Register #(.width(32)) Registro_31 (.D(Data_Input), .en(Input_31), .Q(SP), .clk(in_4), .clr(in_5));

  // Other names for the same wires on the sheet: A1[4:0] = Selector_A; A2[4:0] = Selector_B;
  //   A3[4:0] = Destination_Adress; Clock = in_4; Registro_31[31:0] = SP; Reset = in_5; WD3[31:0] = Data_Input;
  //   WE3 = Read_Write

  // Notes on the sheet:
  //   Register File
endmodule

module LittleEndian_BigEndian (
  input  [31:0] in_1,
  output [31:0] Output
);


  assign Output = {in_1[7:0], in_1[15:8], in_1[23:16], in_1[31:24]};
endmodule

module Instruction_Decoder (
  input  [31:0] Instruction,
  output [5:0] Output,
  output [25:0] Output_2,
  output [4:0] Output_3,
  output [4:0] Output_4,
  output [15:0] Output_5,
  output [4:0] Output_6,
  output [4:0] Output_7,
  output [5:0] Output_8
);


  assign Output = Instruction[31:26];
  assign Output_2 = Instruction[25:0];
  assign Output_3 = Instruction[25:21];
  assign Output_4 = Instruction[20:16];
  assign Output_5 = Instruction[15:0];
  assign Output_6 = Instruction[15:11];
  assign Output_7 = Instruction[10:6];
  assign Output_8 = Instruction[5:0];

  // Other names for the same wires on the sheet: Constante[15:0] = Instruction[15:0];
  //   Destino_salto[25:0] = Instruction[25:0]; Func_code[5:0] = Instruction[5:0]; x[4:0] = Instruction[10:6];
  //   Rd[4:0] = Instruction[15:11]; Rt[4:0] = Instruction[20:16]; Rs[4:0] = Instruction[25:21];
  //   OpCode[5:0] = Instruction[31:26]
endmodule

module Branch_Control (
  input  [31:0] RS,
  input  [31:0] PC,
  input  [25:0] Destino,
  input  [15:0] Offset,
  input  [1:0] BS,
  output [31:0] PC_star
);

  wire [15:0] multiplier_1_out;
  wire [31:0] bit_extender_1_out, PC__4, PC__4_Offset_4;
  wire [31:28] Jump;

  Adder #(.width(32)) adder_1 (.a(PC), .b(32'h4), .out(PC__4));  // open: cin, cout
  Multiplier #(.width(16)) multiplier_1 (.a(Offset), .b(16'h4), .out(multiplier_1_out));  // open: cin, cout
  assign bit_extender_1_out = {{16{multiplier_1_out[15]}}, multiplier_1_out};  // Bit_Extender bit_extender_1
  Adder #(.width(32)) adder_2 (.a(PC__4), .b(bit_extender_1_out), .out(PC__4_Offset_4));  // open: cin, cout
  Multiplexer #(.select(2), .width(32), .enable("false")) multiplexer_1 (
    .in0(PC__4), .in1(PC__4_Offset_4), .in2({Jump, Destino, 2'b00}), .in3(RS), .out(PC_star), .sel(BS));

  // Other names for the same wires on the sheet: Jump[27:2] = Destino
endmodule

module ALU (
  input  [3:0] in_1,
  input  in_2,
  input  [31:0] in_3,
  input  [31:0] in_4,
  output [31:0] HIGH,
  output [31:0] ALU_OUTPUT,
  output [31:0] LOW,
  output ZF,
  output SF,
  output EQF
);

  wire comparator_1_lt, comparator_2_lt, ENABLE_HIGH_LOW;
  wire [1:0] SELECTOR_MUL_DIV;
  wire [31:0] ADD, AND, div_1_high_output, div_1_low_output, divider_1_out, divider_1_rem, mul_1_high_output,
       mul_1_low_output, multiplexer_1_out, multiplexer_2_out, multiplier_1_cout, multiplier_1_out, NOR, OR,
       SLT, SLTU, SUB, XOR;

  assign AND = in_3 & in_4;  // AND_Gate and_1, 32 bits wide
  assign OR = in_3 | in_4;  // OR_Gate or_1, 32 bits wide
  assign NOR = ~(in_3 | in_4);  // NOR_Gate nor_1, 32 bits wide
  assign XOR = in_3 ^ in_4;  // XOR_Gate xor_1, 32 bits wide
  Comparator #(.width(32)) comparator_1 (.a(in_3), .b(in_4), .eq(EQF), .lt(comparator_1_lt));  // open: gt
  Comparator #(.width(32), .mode("unsigned")) comparator_2 (.a(in_3), .b(in_4), .lt(comparator_2_lt));  // open: gt, eq
  Adder #(.width(32)) adder_1 (.a(in_3), .b(in_4), .out(ADD));  // open: cin, cout
  Subtractor #(.width(32)) subtractor_1 (.a(in_3), .b(in_4), .out(SUB));  // open: bin, bout
  Multiplier #(.width(32)) multiplier_1 (
    .a(in_3), .b(in_4), .out(multiplier_1_out), .cout(multiplier_1_cout));  // open: cin
  Divider #(.width(32)) divider_1 (.a(in_3), .b(in_4), .out(divider_1_out), .rem(divider_1_rem));  // open: upper
  DIV div_1 (.in_1(in_3), .in_2(in_4), .Low_Output(div_1_low_output), .High_Output(div_1_high_output));
  MUL mul_1 (.in_1(in_3), .in_2(in_4), .Low_Output(mul_1_low_output), .High_Output(mul_1_high_output));
  assign SLT = {{31{1'b0}}, comparator_1_lt};  // Bit_Extender bit_extender_1
  assign SLTU = {{31{1'b0}}, comparator_2_lt};  // Bit_Extender bit_extender_2
  Multiplexer #(.select(2), .width(32), .enable("false")) multiplexer_1 (
    .in0(multiplier_1_cout), .in1(divider_1_rem), .in2(div_1_high_output), .in3(mul_1_high_output),
    .out(multiplexer_1_out), .sel(SELECTOR_MUL_DIV));
  Multiplexer #(.select(2), .width(32), .enable("false")) multiplexer_2 (
    .in0(multiplier_1_out), .in1(divider_1_out), .in2(div_1_low_output), .in3(mul_1_low_output),
    .out(multiplexer_2_out), .sel(SELECTOR_MUL_DIV));
  Multiplexer #(.select(4), .width(32), .enable("false")) multiplexer_3 (
    .in0(AND), .in1(OR), .in2(NOR), .in3(XOR), .in4(SLT), .in5(SLTU), .in6(ADD), .in7(SUB), .out(ALU_OUTPUT),
    .sel(in_1));  // open: in8, in9, in10, in11, in12, in13, in14, in15
  Comparator #(.width(32)) comparator_3 (.a(in_3), .b({32{1'b0}}), .eq(ZF), .lt(SF));  // open: gt
  and and_2 (ENABLE_HIGH_LOW, in_1[3], ~in_1[2]);  // AND_Gate
  and and_3 (SELECTOR_MUL_DIV[1], in_1[3], ~in_1[2], in_1[1]);  // AND_Gate
  and and_4 (SELECTOR_MUL_DIV[0], in_1[3], ~in_1[2], in_1[0]);  // AND_Gate
  Register #(.width(32)) register_1 (.D(multiplexer_1_out), .en(ENABLE_HIGH_LOW), .Q(HIGH), .clk(in_2));  // open: clr
  Register #(.width(32)) register_2 (.D(multiplexer_2_out), .en(ENABLE_HIGH_LOW), .Q(LOW), .clk(in_2));  // open: clr

  // Other names for the same wires on the sheet: ALU_SELECTOR[3:0] = in_1; CLK = in_2; X[31:0] = in_3; Y[31:0] = in_4

  // Notes on the sheet:
  //   ALU
endmodule

module MUL (
  input  [31:0] in_1,
  input  [31:0] in_2,
  output [31:0] Low_Output,
  output [31:0] High_Output
);

  wire xor_1_out;
  wire [31:0] multiplexer_1_out, multiplexer_2_out, multiplier_1_out, negator_1_out, negator_2_out,
       negator_3_out;

  Negator #(.width(32)) negator_1 (.in(in_1), .out(negator_1_out));
  // Probe on in_1
  Negator #(.width(32)) negator_2 (.in(in_2), .out(negator_2_out));
  // Probe on in_2
  Multiplexer #(.width(32), .enable("false")) multiplexer_1 (
    .in0(in_1), .in1(negator_1_out), .out(multiplexer_1_out), .sel(in_1[31]));
  // Probe on negator_1_out
  Multiplexer #(.width(32), .enable("false")) multiplexer_2 (
    .in0(in_2), .in1(negator_2_out), .out(multiplexer_2_out), .sel(in_2[31]));
  // Probe on negator_2_out
  xor xor_1 (xor_1_out, in_1[31], in_2[31]);
  Multiplier #(.width(32)) multiplier_1 (
    .a(multiplexer_1_out), .b(multiplexer_2_out), .out(multiplier_1_out), .cout(High_Output));  // open: cin
  Negator #(.width(32)) negator_3 (.in(multiplier_1_out), .out(negator_3_out));
  // Probe on Low_Output
  Multiplexer #(.width(32), .enable("false")) multiplexer_3 (
    .in0(multiplier_1_out), .in1(negator_3_out), .out(Low_Output), .sel(xor_1_out));
  // Probe on High_Output

  // Notes on the sheet:
  //   Signed Multiplier
endmodule

module DIV (
  input  [31:0] in_1,
  input  [31:0] in_2,
  output [31:0] Low_Output,
  output [31:0] High_Output
);

  wire xor_1_out;
  wire [31:0] divider_1_out, multiplexer_1_out, multiplexer_2_out, negator_1_out, negator_2_out,
       negator_3_out;

  Negator #(.width(32)) negator_1 (.in(in_1), .out(negator_1_out));
  // Probe on in_1
  Negator #(.width(32)) negator_2 (.in(in_2), .out(negator_2_out));
  // Probe on in_2
  Multiplexer #(.width(32), .enable("false")) multiplexer_1 (
    .in0(in_1), .in1(negator_1_out), .out(multiplexer_1_out), .sel(in_1[31]));
  // Probe on negator_1_out
  Multiplexer #(.width(32), .enable("false")) multiplexer_2 (
    .in0(in_2), .in1(negator_2_out), .out(multiplexer_2_out), .sel(in_2[31]));
  // Probe on negator_2_out
  xor xor_1 (xor_1_out, in_1[31], in_2[31]);
  Divider #(.width(32)) divider_1 (
    .a(multiplexer_1_out), .b(multiplexer_2_out), .out(divider_1_out), .rem(High_Output));  // open: upper
  Negator #(.width(32)) negator_3 (.in(divider_1_out), .out(negator_3_out));
  // Probe on Low_Output
  Multiplexer #(.width(32), .enable("false")) multiplexer_3 (
    .in0(divider_1_out), .in1(negator_3_out), .out(Low_Output), .sel(xor_1_out));
  // Probe on High_Output

  // Notes on the sheet:
  //   Signed Divider
endmodule

module ALU_Encoder (
  input  ADD,
  input  ADDI,
  input  SUB,
  input  MULT,
  input  MULU,
  input  DIV,
  input  DIVU,
  input  SLT,
  input  SLTI,
  input  SLTU,
  input  SLTIU,
  input  AND,
  input  ANDI,
  input  OR,
  input  ORI,
  input  XOR,
  input  XORI,
  input  NOR,
  output Type_I,
  output [3:0] ALU_SELECTOR
);

  wire ADD_t, AND_t, OR_t, SLT_t, SLTU_t, XOR_t;

  or or_1 (ADD_t, ADD, ADDI);
  or or_2 (SLT_t, SLT, SLTI);
  or or_3 (SLTU_t, SLTU, SLTIU);
  or or_4 (AND_t, AND, ANDI);
  or or_5 (OR_t, OR, ORI);
  or or_6 (XOR_t, XOR, XORI);
  or or_7 (Type_I, ADDI, SLTI, SLTIU, ANDI, ORI, XORI);
  or or_8 (ALU_SELECTOR[3], MULT, DIVU, DIV, MULU);
  or or_9 (ALU_SELECTOR[2], SLT_t, SLTU_t, ADD_t, SUB);
  or or_10 (ALU_SELECTOR[1], NOR, XOR_t, ADD_t, SUB, DIV, MULU);
  or or_11 (ALU_SELECTOR[0], OR_t, XOR_t, SLTU_t, SUB, DIVU, MULU);

  // Notes on the sheet:
  //   ALU Encoder
endmodule

module Write_to_Ram (
  input  [31:0] MEMORY,
  input  [31:0] VALUE,
  output [3:0] MASK,
  output [31:0] INPUT0,
  output [15:0] ADDRESS,
  output [31:0] INPUT1,
  output [31:0] INPUT2,
  output [31:0] INPUT3
);

  wire [31:0] littleendian_bigendian_1_output;

  Demultiplexer #(.select(2), .enable("false")) demultiplexer_1 (
    .out0(MASK[0]), .out1(MASK[1]), .out2(MASK[2]), .out3(MASK[3]), .in(1'b1), .sel(MEMORY[3:2]));
  Demultiplexer #(.select(2), .width(32), .enable("false")) demultiplexer_2 (
    .out0(INPUT0), .out1(INPUT1), .out2(INPUT2), .out3(INPUT3), .in(littleendian_bigendian_1_output),
    .sel(MEMORY[3:2]));
  LittleEndian_BigEndian littleendian_bigendian_1 (.in_1(VALUE), .Output(littleendian_bigendian_1_output));

  assign ADDRESS = MEMORY[19:4];

  // Other names for the same wires on the sheet: SELECTOR[1:0] = MEMORY[3:2]
endmodule

module Read_from_Ram (
  input  [31:0] BANK0,
  input  [31:0] BANK1,
  input  [31:0] BANK2,
  input  [31:0] BANK3,
  input  [31:0] MEMORY,
  output [31:0] RAM_DATA
);

  wire [31:0] multiplexer_1_out;

  Multiplexer #(.select(2), .width(32), .enable("false")) multiplexer_1 (
    .in0(BANK0), .in1(BANK1), .in2(BANK2), .in3(BANK3), .out(multiplexer_1_out), .sel(MEMORY[3:2]));
  LittleEndian_BigEndian littleendian_bigendian_1 (.in_1(multiplexer_1_out), .Output(RAM_DATA));

  // Other names for the same wires on the sheet: SELECTOR[1:0] = MEMORY[3:2]
endmodule

module Timer (
  input  [3:0] in_1,
  input  in_2,
  input  in_3,
  input  in_4,
  output Output
);

  wire [3:0] counter_1_q;

  Counter #(.width(4), .max('hf)) counter_1 (
    .count(in_2), .Q(counter_1_q), .clk(in_3), .clr(in_4));  // open: load, D, carry
  Comparator #(.width(4)) comparator_1 (.a(in_1), .b(counter_1_q), .eq(Output));  // open: gt, lt
endmodule
